// Logisim project maybeProject.circ as structural Verilog
// 12
module main (
  input  [31:0] in_1,
  input  [31:0] in_2,
  input  [31:0] in_3,
  input  [31:0] in_4,
  input  [31:0] in_5,
  input  [31:0] in_6,
  input  [31:0] in_7,
  input  [31:0] in_8,
  input  [31:0] in_9,
  input  [31:0] in_10,
  input  [31:0] in_11,
  input  [31:0] in_12,
  input  [31:0] in_13,
  input  [31:0] in_14,
  input  [31:0] in_15,
  input  [31:0] in_16,
  input  [31:0] in_17,
  input  [31:0] in_18,
  input  [31:0] in_19,
  input  [31:0] in_20,
  input  [31:0] in_21,
  input  [31:0] in_22,
  input  [31:0] in_23,
  input  [31:0] in_24,
  input  [31:0] in_25,
  input  [31:0] in_26,
  input  [31:0] in_27,
  input  [31:0] in_28,
  input  [31:0] in_29,
  input  [31:0] in_30,
  input  [31:0] in_31,
  input  [31:0] in_32
);

  wire button_1_out, clock_1_out;
  wire [31:0] _1, _2, _3, _4, _5, _6, _8, _9, _10, _11, _12, _13, _14, _15, _16, _17, _18, _19, _20, _21,
       _22, _23, _24, _25, _26, _27, _28, _29, _30, _31, _32, walk_1_aout, walk_1_bout;

  DotMatrix #(.matrixcols(32), .matrixrows(32)) dotmatrix_1 (
    .col0(_1), .col1(_2), .col2(_3), .col3(_4), .col4(_5), .col5(_6), .col6(in_7), .col7(_8), .col8(_9),
    .col9(_10), .col10(_11), .col11(_12), .col12(_13), .col13(_14), .col14(_15), .col15(_16), .col16(_17),
    .col17(_18), .col18(_19), .col19(_20), .col20(_21), .col21(_22), .col22(_23), .col23(_24), .col24(_25),
    .col25(_26), .col26(_27), .col27(_28), .col28(_29), .col29(_30), .col30(_31), .col31(_32));
  jump jump_1 (.clock(button_1_out), .in(in_1), .out(_1));
  jump jump_2 (.clock(button_1_out), .in(walk_1_bout), .out(_5));
  jump jump_3 (.clock(button_1_out), .in(in_2), .out(_2));
  jump jump_4 (.clock(button_1_out), .in(walk_1_aout), .out(_3));
  walk walk_1 (.clock(clock_1_out), .A(in_3), .B(in_5), .Aout(walk_1_aout), .Bout(walk_1_bout));
  jump jump_5 (.clock(button_1_out), .in(in_4), .out(_4));
  Clock clock_1 (.out(clock_1_out));
  jump jump_6 (.clock(button_1_out), .in(in_6), .out(_6));
  Button button_1 (.out(button_1_out));
  mover mover_1 (
    .in_1(clock_1_out), .out_3(_32), .out_4(_31), .out_5(_30), .out_6(_29), .out_7(_28), .out_8(_27),
    .out_9(_26), .out_10(_25), .out_11(_24), .out_12(_23), .out_13(_22), .out_14(_21), .out_15(_20),
    .out_16(_19), .out_17(_18), .out_18(_17), .out_19(_16), .out_20(_15), .out_21(_14), .out_22(_13),
    .out_23(_12), .out_24(_11), .out_25(_10), .out_26(_9), .out_27(_8));  // open: in_2

  // Other names for the same wires on the sheet: _7[31:0] = in_7; vec_adr[31:0] = in_32
endmodule

module walk (
  input  clock,
  input  [31:0] A,
  input  [31:0] B,
  output [31:0] Aout,
  output [31:0] Bout
);

  wire [1:1] not_1_out, not_2_out;

  not not_1 (not_1_out[1], A[1]);
  not not_2 (not_2_out[1], B[1]);
  Multiplexer #(.width(32)) multiplexer_1 (
    .in0({B[31:2], not_2_out[1], B[0]}), .in1(B), .out(Bout), .sel(clock));  // open: en
  Multiplexer #(.width(32)) multiplexer_2 (
    .in0(A), .in1({A[31:2], not_1_out[1], A[0]}), .out(Aout), .sel(clock));  // open: en
endmodule

module jump (
  input  clock,
  input  [31:0] in,
  output [31:0] out
);

  wire [0:0] multiplexer_1_out, not_1_out;
  wire [31:0] shifter_1_out;

  not not_1 (not_1_out[0], in[0]);
  Multiplexer #(.width(32)) multiplexer_1 (
    .in0({in[31:1], not_1_out[0]}), .in1(shifter_1_out), .out({out[31:1], multiplexer_1_out[0]}), .sel(clock));  // open: en
  Shifter #(.width(32), .shift("rl")) shifter_1 (.in({in[31:1], not_1_out[0]}), .\dist (5'b00001), .out(shifter_1_out));
  not not_2 (out[0], multiplexer_1_out[0]);
endmodule

module mover (
  input  in_1,
  input  [31:0] in_2,
  output [31:0] out_3,
  output [31:0] out_4,
  output [31:0] out_5,
  output [31:0] out_6,
  output [31:0] out_7,
  output [31:0] out_8,
  output [31:0] out_9,
  output [31:0] out_10,
  output [31:0] out_11,
  output [31:0] out_12,
  output [31:0] out_13,
  output [31:0] out_14,
  output [31:0] out_15,
  output [31:0] out_16,
  output [31:0] out_17,
  output [31:0] out_18,
  output [31:0] out_19,
  output [31:0] out_20,
  output [31:0] out_21,
  output [31:0] out_22,
  output [31:0] out_23,
  output [31:0] out_24,
  output [31:0] out_25,
  output [31:0] out_26,
  output [31:0] out_27
);

  wire comparator_1_eq, not_1_out;
  wire [31:0] multiplexer_1_out;

  Multiplexer #(.width(32)) multiplexer_1 (
    .in0(32'h1), .in1(in_2), .out(multiplexer_1_out), .sel(not_1_out));  // open: en
  not not_1 (not_1_out, comparator_1_eq);
  Comparator #(.width(32)) comparator_1 (.a(in_2), .b({32{1'b0}}), .eq(comparator_1_eq));  // open: gt, lt
  Pull_Resistor #(.pull(1)) pull_resistor_1 (.node(comparator_1_eq));
  Register #(.width(32)) register_1 (.D(multiplexer_1_out), .Q(out_3), .clk(in_1));  // open: en, clr
  Register #(.width(32)) register_2 (.D(out_3), .Q(out_4), .clk(in_1));  // open: en, clr
  Register #(.width(32)) register_3 (.D(out_4), .Q(out_5), .clk(in_1));  // open: en, clr
  Register #(.width(32)) register_4 (.D(out_5), .Q(out_6), .clk(in_1));  // open: en, clr
  Register #(.width(32)) register_5 (.D(out_6), .Q(out_7), .clk(in_1));  // open: en, clr
  Register #(.width(32)) register_6 (.D(out_7), .Q(out_8), .clk(in_1));  // open: en, clr
  Register #(.width(32)) register_7 (.D(out_8), .Q(out_9), .clk(in_1));  // open: en, clr
  Register #(.width(32)) register_8 (.D(out_9), .Q(out_10), .clk(in_1));  // open: en, clr
  Register #(.width(32)) register_9 (.D(out_10), .Q(out_11), .clk(in_1));  // open: en, clr
  Register #(.width(32)) register_10 (.D(out_11), .Q(out_12), .clk(in_1));  // open: en, clr
  Register #(.width(32)) register_11 (.D(out_12), .Q(out_13), .clk(in_1));  // open: en, clr
  Register #(.width(32)) register_12 (.D(out_13), .Q(out_14), .clk(in_1));  // open: en, clr
  Register #(.width(32)) register_13 (.D(out_14), .Q(out_15), .clk(in_1));  // open: en, clr
  Register #(.width(32)) register_14 (.D(out_15), .Q(out_16), .clk(in_1));  // open: en, clr
  Register #(.width(32)) register_15 (.D(out_16), .Q(out_17), .clk(in_1));  // open: en, clr
  Register #(.width(32)) register_16 (.D(out_17), .Q(out_18), .clk(in_1));  // open: en, clr
  Register #(.width(32)) register_17 (.D(out_18), .Q(out_19), .clk(in_1));  // open: en, clr
  Register #(.width(32)) register_18 (.D(out_19), .Q(out_20), .clk(in_1));  // open: en, clr
  Register #(.width(32)) register_19 (.D(out_20), .Q(out_21), .clk(in_1));  // open: en, clr
  Register #(.width(32)) register_20 (.D(out_21), .Q(out_22), .clk(in_1));  // open: en, clr
  Register #(.width(32)) register_21 (.D(out_22), .Q(out_23), .clk(in_1));  // open: en, clr
  Register #(.width(32)) register_22 (.D(out_23), .Q(out_24), .clk(in_1));  // open: en, clr
  Register #(.width(32)) register_23 (.D(out_24), .Q(out_25), .clk(in_1));  // open: en, clr
  Register #(.width(32)) register_24 (.D(out_25), .Q(out_26), .clk(in_1));  // open: en, clr
  Register #(.width(32)) register_25 (.D(out_26), .Q(out_27), .clk(in_1));  // open: en, clr
endmodule
